// Logisim project LALU.circ as structural Verilog: 3 circuits, main circuit main
module main (
  input  rst,
  input  subtract,
  input  [1:0] Rd,
  input  [1:0] Rs,
  output [15:0] out_5,
  output [15:0] out_6,
  output [15:0] out_7,
  output [15:0] out_8
);

  wire clk, csbasedaddsubtract_1_overflow, register_1_q, regwe_1_reg0we, regwe_1_reg1we, regwe_1_reg2we,
       regwe_1_reg3we;
  wire [15:0] csbasedaddsubtract_1_sum, srcsel_1_regout, srcsel_2_regout;

  Clock clock_1 (.out(clk));
  srcSel srcsel_1 (.reg1(out_6), .reg2(out_7), .reg3(out_8), .sel(Rd), .reg0(out_5), .regOut(srcsel_1_regout));
  srcSel srcsel_2 (.reg1(out_6), .reg2(out_7), .reg3(out_8), .sel(Rs), .reg0(out_5), .regOut(srcsel_2_regout));
  CSBasedAddSubtract csbasedaddsubtract_1 (
    .OP(subtract), .A(srcsel_1_regout), .B(srcsel_2_regout), .Sum(csbasedaddsubtract_1_sum),
    .Overflow(csbasedaddsubtract_1_overflow));
  regWE regwe_1 (
    .Rd(Rd), .regWrite(1'b1), .reg0WE(regwe_1_reg0we), .reg1WE(regwe_1_reg1we), .reg2WE(regwe_1_reg2we),
    .reg3WE(regwe_1_reg3we));
  Register #(.width(16)) R0 (.D(csbasedaddsubtract_1_sum), .en(regwe_1_reg0we), .clk(clk), .Q(out_5), .clr(rst));
  Register #(.width(16)) R1 (.D(csbasedaddsubtract_1_sum), .en(regwe_1_reg1we), .clk(clk), .Q(out_6), .clr(rst));
  Register #(.width(16)) R2 (.D(csbasedaddsubtract_1_sum), .en(regwe_1_reg2we), .clk(clk), .Q(out_7), .clr(rst));
  Register #(.width(16)) R3 (.D(csbasedaddsubtract_1_sum), .en(regwe_1_reg3we), .clk(clk), .Q(out_8), .clr(rst));
  Register #(.width(1)) register_1 (
    .D(1'b1), .en(csbasedaddsubtract_1_overflow), .clk(clk), .Q(register_1_q), .clr(rst));
  LED led_1 (.in(register_1_q));

  // Other names for the same wires on the sheet: R0[15:0] = out_5; R1[15:0] = out_6; R2[15:0] = out_7;
  //   R3[15:0] = out_8
endmodule

module regWE (
  input  regWrite,
  input  [1:0] Rd,
  output reg0WE,
  output reg1WE,
  output reg2WE,
  output reg3WE
);

  wire and_1_out, and_2_out, and_3_out, nor_1_out, not_1_out, not_2_out;

  not not_1 (not_1_out, Rd[1]);
  not not_2 (not_2_out, Rd[0]);
  nor nor_1 (nor_1_out, Rd[0], Rd[1]);
  and and_1 (and_1_out, Rd[0], not_1_out);
  and and_2 (and_2_out, not_2_out, Rd[1]);
  and and_3 (and_3_out, Rd[0], Rd[1]);
  and and_4 (reg0WE, nor_1_out, regWrite);
  and and_5 (reg1WE, and_1_out, regWrite);
  and and_6 (reg2WE, and_2_out, regWrite);
  and and_7 (reg3WE, and_3_out, regWrite);
endmodule

module srcSel (
  input  [1:0] sel,
  input  [15:0] reg0,
  input  [15:0] reg1,
  input  [15:0] reg2,
  input  [15:0] reg3,
  output [15:0] regOut
);

  Multiplexer #(.select(2), .width(16)) multiplexer_1 (
    .in0(reg0), .in1(reg1), .in2(reg2), .in3(reg3), .out(regOut), .sel(sel));
endmodule
